// Logisim project hw4.circ as structural Verilog
module ALU (
  input  [15:0] a,
  input  [15:0] b,
  input  [2:0] shift,
  input  [3:0] ALUop,
  output [15:0] Result,
  output bigOR,
  output lastbit
);

  wire [14:0] subtractor_1_out;
  wire [15:0] adder_1_out, not_1_out, or_1_out, shifter_1_out, shifter_2_out, xor_1_out;

  assign not_1_out = ~a;  // NOT_Gate not_1, 16 bits wide
  assign xor_1_out = a ^ b;  // XOR_Gate xor_1, 16 bits wide
  Adder #(.width(16)) adder_1 (.a(a), .b(b), .out(adder_1_out));  // open: cin, cout
  Subtractor #(.width(16)) subtractor_1 (.a(a), .b(b), .out({lastbit, subtractor_1_out}));  // open: bin, bout
  Shifter #(.width(16), .shift("ar")) shifter_1 (.in(a), .\dist ({shift, 1'b0}), .out(shifter_1_out));
  Shifter #(.width(16)) shifter_2 (.in(a), .\dist ({shift, 1'b0}), .out(shifter_2_out));
  Multiplexer #(.select(4), .width(16)) multiplexer_1 (
    .in0(not_1_out), .in1(xor_1_out), .in2(adder_1_out), .in3(adder_1_out),
    .in4({lastbit, subtractor_1_out}), .in5(shifter_1_out), .in6(shifter_2_out), .in7(adder_1_out),
    .in8(adder_1_out), .out(Result), .sel(ALUop));  // open: in9, in10, in11, in12, in13, in14, in15, en
  assign or_1_out = {lastbit, subtractor_1_out} | {16{1'b0}};  // OR_Gate or_1, 16 bits wide
  or or_2 (bigOR, or_1_out[0], or_1_out[1], or_1_out[2], or_1_out[3], or_1_out[4], or_1_out[5], or_1_out[6], or_1_out[7], or_1_out[8], or_1_out[9], or_1_out[10], or_1_out[11], or_1_out[12], or_1_out[13], or_1_out[14], or_1_out[15]);
endmodule

module RegisterFile (
  input  [2:0] ReadReg1,
  input  [2:0] ReadReg2,
  input  [15:0] WriteData,
  input  [2:0] WriteReg,
  input  Clock,
  input  RegWriteEnable,
  input  Reset,
  output [15:0] ReadData1,
  output [15:0] ReadData2
);

  wire and_1_out, and_2_out, and_3_out, and_4_out, and_5_out, and_6_out, and_7_out, clock_t, read1_0,
       read1_1, read1_2, read1_3, read1_4, read1_5, read1_6, read1_7, read2_0, read2_1, read2_2, read2_3,
       read2_4, read2_5, read2_6, read2_7, write1, write2, write3, write4, write5, write6, write7;
  wire [15:0] register_1_q, register_2_q, register_3_q, register_4_q, register_5_q, register_6_q,
       register_7_q, register_8_q;

  Decoder #(.select(3), .enable("false")) decoder_1 (
    .out0(read1_0), .out1(read1_1), .out2(read1_2), .out3(read1_3), .out4(read1_4), .out5(read1_5),
    .out6(read1_6), .out7(read1_7), .sel(ReadReg1));
  Decoder #(.select(3), .enable("false")) decoder_2 (
    .out0(read2_0), .out1(read2_1), .out2(read2_2), .out3(read2_3), .out4(read2_4), .out5(read2_5),
    .out6(read2_6), .out7(read2_7), .sel(ReadReg2));
  Decoder #(.select(3), .enable("false")) decoder_3 (
    .out1(write1), .out2(write2), .out3(write3), .out4(write4), .out5(write5), .out6(write6), .out7(write7),
    .sel(WriteReg));  // open: out0
  and and_1 (and_1_out, write1, RegWriteEnable);
  and and_2 (and_2_out, write2, RegWriteEnable);
  and and_3 (and_3_out, write3, RegWriteEnable);
  and and_4 (and_4_out, write4, RegWriteEnable);
  and and_5 (and_5_out, write5, RegWriteEnable);
  and and_6 (and_6_out, write6, RegWriteEnable);
  and and_7 (and_7_out, write7, RegWriteEnable);
  Register #(.width(16), .trigger("falling")) register_1 (
    .D({16{1'b0}}), .Q(register_1_q), .clk(clock_t), .clr(Reset));  // open: en
  Register #(.width(16), .trigger("falling")) register_2 (
    .D(WriteData), .en(and_1_out), .Q(register_2_q), .clk(clock_t), .clr(Reset));
  Register #(.width(16), .trigger("falling")) register_3 (
    .D(WriteData), .en(and_2_out), .Q(register_3_q), .clk(clock_t), .clr(Reset));
  Register #(.width(16), .trigger("falling")) register_4 (
    .D(WriteData), .en(and_3_out), .Q(register_4_q), .clk(clock_t), .clr(Reset));
  Register #(.width(16), .trigger("falling")) register_5 (
    .D(WriteData), .en(and_4_out), .Q(register_5_q), .clk(clock_t), .clr(Reset));
  Register #(.width(16), .trigger("falling")) register_6 (
    .D(WriteData), .en(and_5_out), .Q(register_6_q), .clk(clock_t), .clr(Reset));
  Register #(.width(16), .trigger("falling")) register_7 (
    .D(WriteData), .en(and_6_out), .Q(register_7_q), .clk(clock_t), .clr(Reset));
  Register #(.width(16), .trigger("falling")) register_8 (
    .D(WriteData), .en(and_7_out), .Q(register_8_q), .clk(clock_t), .clr(Reset));
  // Probe on nothing
  // Probe on nothing
  // Probe on nothing
  // Probe on nothing
  // Probe on nothing
  // Probe on nothing
  // Probe on nothing
  // Probe on nothing
  assign ReadData1 = read1_0 ? register_1_q : 16'bz;  // Controlled_Buffer controlled_buffer_1
  assign ReadData2 = read2_0 ? register_1_q : 16'bz;  // Controlled_Buffer controlled_buffer_2
  assign ReadData1 = read1_1 ? register_2_q : 16'bz;  // Controlled_Buffer controlled_buffer_3
  assign ReadData2 = read2_1 ? register_2_q : 16'bz;  // Controlled_Buffer controlled_buffer_4
  assign ReadData1 = read1_2 ? register_3_q : 16'bz;  // Controlled_Buffer controlled_buffer_5
  assign ReadData2 = read2_2 ? register_3_q : 16'bz;  // Controlled_Buffer controlled_buffer_6
  assign ReadData1 = read1_3 ? register_4_q : 16'bz;  // Controlled_Buffer controlled_buffer_7
  assign ReadData2 = read2_3 ? register_4_q : 16'bz;  // Controlled_Buffer controlled_buffer_8
  assign ReadData1 = read1_4 ? register_5_q : 16'bz;  // Controlled_Buffer controlled_buffer_9
  assign ReadData2 = read2_4 ? register_5_q : 16'bz;  // Controlled_Buffer controlled_buffer_10
  assign ReadData1 = read1_5 ? register_6_q : 16'bz;  // Controlled_Buffer controlled_buffer_11
  assign ReadData2 = read2_5 ? register_6_q : 16'bz;  // Controlled_Buffer controlled_buffer_12
  assign ReadData1 = read1_6 ? register_7_q : 16'bz;  // Controlled_Buffer controlled_buffer_13
  assign ReadData2 = read2_6 ? register_7_q : 16'bz;  // Controlled_Buffer controlled_buffer_14
  assign ReadData1 = read1_7 ? register_8_q : 16'bz;  // Controlled_Buffer controlled_buffer_15
  assign ReadData2 = read2_7 ? register_8_q : 16'bz;  // Controlled_Buffer controlled_buffer_16

  // Other names for the same wires on the sheet: E = RegWriteEnable
endmodule

module pc (
  input  [15:0] \input ,
  input  clk,
  input  reset,
  output [15:0] \output 
);

  D_Flip_Flop d_ff_1 (.clk(clk), .D(\input [0]), .Q(\output [0]), .en(1'b1), .reset(reset));  // open: Qn, preset
  D_Flip_Flop d_ff_2 (.clk(clk), .D(\input [1]), .Q(\output [1]), .en(1'b1), .reset(reset));  // open: Qn, preset
  D_Flip_Flop d_ff_3 (.clk(clk), .D(\input [2]), .Q(\output [2]), .en(1'b1), .reset(reset));  // open: Qn, preset
  D_Flip_Flop d_ff_4 (.clk(clk), .D(\input [3]), .Q(\output [3]), .en(1'b1), .reset(reset));  // open: Qn, preset
  D_Flip_Flop d_ff_5 (.clk(clk), .D(\input [4]), .Q(\output [4]), .en(1'b1), .reset(reset));  // open: Qn, preset
  D_Flip_Flop d_ff_6 (.clk(clk), .D(\input [5]), .Q(\output [5]), .en(1'b1), .reset(reset));  // open: Qn, preset
  D_Flip_Flop d_ff_7 (.clk(clk), .D(\input [6]), .Q(\output [6]), .en(1'b1), .reset(reset));  // open: Qn, preset
  D_Flip_Flop d_ff_8 (.clk(clk), .D(\input [7]), .Q(\output [7]), .en(1'b1));  // open: Qn, preset, reset
  D_Flip_Flop d_ff_9 (.clk(clk), .D(\input [8]), .Q(\output [8]), .en(1'b1), .reset(reset));  // open: Qn, preset
  D_Flip_Flop d_ff_10 (.clk(clk), .D(\input [9]), .Q(\output [9]), .en(1'b1), .reset(reset));  // open: Qn, preset
  D_Flip_Flop d_ff_11 (.clk(clk), .D(\input [10]), .Q(\output [10]), .en(1'b1), .reset(reset));  // open: Qn, preset
  D_Flip_Flop d_ff_12 (.clk(clk), .D(\input [11]), .Q(\output [11]), .en(1'b1), .reset(reset));  // open: Qn, preset
  D_Flip_Flop d_ff_13 (.clk(clk), .D(\input [12]), .Q(\output [12]), .en(1'b1), .reset(reset));  // open: Qn, preset
  D_Flip_Flop d_ff_14 (.clk(clk), .D(\input [13]), .Q(\output [13]), .en(1'b1), .reset(reset));  // open: Qn, preset
  D_Flip_Flop d_ff_15 (.clk(clk), .D(\input [14]), .Q(\output [14]), .en(1'b1), .reset(reset));  // open: Qn, preset
  D_Flip_Flop d_ff_16 (.clk(clk), .D(\input [15]), .Q(\output [15]), .en(1'b1), .reset(reset));  // open: Qn, preset
endmodule

module _1 (
  input  [15:0] Address,
  output [15:0] new_address
);

  Adder #(.width(16)) adder_1 (.a(16'h1), .b(Address), .out(new_address));  // open: cin, cout
endmodule
